// Logisim project MPU.circ as structural Verilog: 4 circuits, main circuit MPU
module PC (
  input  [7:0] I,
  input  J,
  input  CLK,
  input  CLR,
  input  CE,
  output [7:0] O
);

  wire [7:0] adder_1_out, multiplexer_1_out, multiplexer_2_out;

  Multiplexer #(.enable("false"), .width(8)) multiplexer_1 (
    .in0(multiplexer_2_out), .in1(I), .out(multiplexer_1_out), .sel(J));
  Register register_1 (.D(multiplexer_1_out), .en(1'b1), .clk(CLK), .Q(O), .clr(CLR));
  Adder adder_1 (.a(O), .b(8'h1), .out(adder_1_out));  // open: cin, cout
  Multiplexer #(.enable("false"), .width(8)) multiplexer_2 (
    .in0(O), .in1(adder_1_out), .out(multiplexer_2_out), .sel(CE));
endmodule

module ALU (
  input  NA,
  input  F,
  input  NO,
  input  [7:0] A,
  input  NB,
  input  [7:0] B,
  output ZF,
  output [7:0] O,
  output CF
);

  wire adder_1_cout, or_1_out;
  wire [7:0] adder_1_out, and_1_out, multiplexer_1_out, multiplexer_2_out, multiplexer_3_out, not_1_out,
       not_2_out, not_3_out;

  assign not_1_out = ~A;  // NOT_Gate not_1, 8 bits wide
  assign not_2_out = ~B;  // NOT_Gate not_2, 8 bits wide
  Multiplexer #(.enable("false"), .width(8)) multiplexer_1 (
    .in0(A), .in1(not_1_out), .out(multiplexer_1_out), .sel(NA));
  Multiplexer #(.enable("false"), .width(8)) multiplexer_2 (
    .in0(B), .in1(not_2_out), .out(multiplexer_2_out), .sel(NB));
  Adder adder_1 (.a(multiplexer_1_out), .b(multiplexer_2_out), .out(adder_1_out), .cout(adder_1_cout));  // open: cin
  assign and_1_out = multiplexer_1_out & multiplexer_2_out;  // AND_Gate and_1, 8 bits wide
  Multiplexer #(.enable("false"), .width(8)) multiplexer_3 (
    .in0(and_1_out), .in1(adder_1_out), .out(multiplexer_3_out), .sel(F));
  assign not_3_out = ~multiplexer_3_out;  // NOT_Gate not_3, 8 bits wide
  and and_2 (CF, adder_1_cout, F);
  Multiplexer #(.enable("false"), .width(8)) multiplexer_4 (
    .in0(multiplexer_3_out), .in1(not_3_out), .out(O), .sel(NO));
  or or_1 (or_1_out, O[7], O[6], O[5], O[4], O[3], O[2], O[1], O[0]);
  not not_4 (ZF, or_1_out);
endmodule

module MCU (
  input  CLR,
  input  PROG,
  input  [7:0] AI,
  input  [7:0] DI,
  input  DBG,
  input  CLK,
  input  ENT,
  output [7:0] REG_A,
  output [1:0] FLG,
  output [7:0] PC,
  output [7:0] REG_B,
  output [7:0] ADDR,
  output [7:0] DISP,
  output [7:0] DATA,
  output [5:0] TMO
);

  wire AI_t, and_1_out, AO, BI, BO, C, CE, CLK_t, CO, decoder_1_out6, EO, F, FI, HLT, II, J, MI,
       multiplexer_1_out, multiplexer_4_out, NA, NB, NO, not_1_out, OI, or_1_out, RI, RO;
  wire [1:0] alu_1_cf;
  wire [2:0] counter_2_q;
  wire [7:0] alu_1_o, BUS8B, multiplexer_3_out, register_1_q, register_2_q;

  Register register_1 (.D(BUS8B), .en(MI), .clk(CLK_t), .Q(register_1_q), .clr(CLR));
  Counter counter_1 (.load(J), .D(BUS8B), .count(CE), .Q(PC), .up(1'b1), .clk(CLK_t), .clr(CLR));  // open: carry
  and and_1 (and_1_out, CLK_t, RI);
  Register register_2 (.D(BUS8B), .en(II), .clk(CLK_t), .Q(register_2_q), .clr(CLR));
  not not_1 (not_1_out, CLK_t);
  or or_1 (or_1_out, CLR, C, decoder_1_out6);
  Multiplexer #(.enable("false")) multiplexer_1 (.in0(CLK), .in1(ENT), .out(multiplexer_1_out), .sel(DBG));
  assign BUS8B = CO ? PC : 8'bz;  // Controlled_Buffer controlled_buffer_1
  Multiplexer #(.enable("false"), .width(8)) multiplexer_2 (.in0(register_1_q), .in1(AI), .out(ADDR), .sel(PROG));
  Multiplexer #(.enable("false"), .width(8)) multiplexer_3 (.in0(BUS8B), .in1(DI), .out(multiplexer_3_out), .sel(PROG));
  Decoder #(.select(3)) decoder_1 (
    .out0(TMO[0]), .out1(TMO[1]), .out2(TMO[2]), .out3(TMO[3]), .out4(TMO[4]), .out5(TMO[5]),
    .out6(decoder_1_out6), .sel(counter_2_q), .en(1'b1));  // open: out7
  Counter #(.max('h7), .width(3)) counter_2 (
    .count(1'b1), .Q(counter_2_q), .up(1'b1), .clk(not_1_out), .clr(or_1_out));  // open: load, D, carry
  and and_2 (CLK_t, multiplexer_1_out, ~HLT);  // AND_Gate
  RAM #(.trigger("high")) ram_1 (.addr(ADDR), .we(multiplexer_4_out), .oe(1'b1), .din(multiplexer_3_out), .dout(DATA));
  Multiplexer #(.enable("false")) multiplexer_4 (.in0(and_1_out), .in1(CLK), .out(multiplexer_4_out), .sel(PROG));
  ROM #(.addrWidth(14), .dataWidth(20)) rom_1 (
    .addr({FLG, register_2_q, 1'b0, counter_2_q}),
    .data({C, OI, FI, EO, NO, F, NB, NA, BO, BI, AO, AI_t, II, RO, RI, MI, HLT, J, CO, CE}));
  assign BUS8B = RO ? DATA : 8'bz;  // Controlled_Buffer controlled_buffer_2
  Register A_REG (.D(BUS8B), .en(AI_t), .clk(CLK_t), .Q(REG_A), .clr(CLR));
  Register B_REG (.D(BUS8B), .en(BI), .clk(CLK_t), .Q(REG_B), .clr(CLR));
  Register register_3 (.D(BUS8B), .en(OI), .clk(CLK_t), .Q(DISP), .clr(CLR));
  assign BUS8B = AO ? REG_A : 8'bz;  // Controlled_Buffer controlled_buffer_3
  assign BUS8B = BO ? REG_B : 8'bz;  // Controlled_Buffer controlled_buffer_4
  ALU alu_1 (.O(alu_1_o), .CF(alu_1_cf[0]), .ZF(alu_1_cf[1]), .A(REG_A), .B(REG_B), .NA(NA), .NB(NB), .F(F), .NO(NO));
  assign BUS8B = EO ? alu_1_o : 8'bz;  // Controlled_Buffer controlled_buffer_5
  Register #(.width(2)) register_4 (.D(alu_1_cf), .en(FI), .clk(CLK_t), .Q(FLG), .clr(CLR));

  // Other names for the same wires on the sheet: CF = FLG[0]; ZF = FLG[1]

  // Notes on the sheet:
  //   PROGRAM COUNTER
  //   IR & CU
  //   MAR & RAM
  //   contents of rom_1 (hex, n*v repeats v):
  //   12 c1 8 80000 12*0 12 c1 12 40041 80000 11*0 12 c1 12 50 40041 80000 10*0 12 c1 40200 80000 12*0 12
  //   c1 40800 80000 204*0 12 c1 12 141 80000 11*0 12 c1 12 441 80000 11*0 12 c1 12 50 141 80000 10*0 12
  //   c1 12 50 441 80000 10*0 12 c1 12 50 221 80000 10*0 12 c1 12 50 821 80000 170*0 12 c1 34100 80000
  //   12*0 12 c1 34400 80000 12*0 12 c1 3d100 80000 12*0 12 c1 3e400 80000 204*0 12 c1 30100 80000 12*0 12
  //   c1 30400 80000 12*0 12 c1 3b100 80000 12*0 12 c1 3b400 80000 204*0 12 c1 12 44 80000 11*0 12 c1 12
  //   50 44 80000 10*0 12 c1 204 80000 12*0 12 c1 804 80000 204*0 12 c1 12 1 80000 11*0 12 c1 12 50 1
  //   80000 10*0 12 c1 1 80000 12*0 12 c1 1 80000 204*0 12 c1 12 1 80000 11*0 12 c1 12 50 1 80000 10*0 12
  //   c1 1 80000 12*0 12 c1 1 80000 2492*0 12 c1 8 80000 12*0 12 c1 12 40041 80000 11*0 12 c1 12 50 40041
  //   80000 10*0 12 c1 40200 80000 12*0 12 c1 40800 80000 204*0 12 c1 12 141 80000 11*0 12 c1 12 441 80000
  //   11*0 12 c1 12 50 141 80000 10*0 12 c1 12 50 441 80000 10*0 12 c1 12 50 221 80000 10*0 12 c1 12 50
  //   821 80000 170*0 12 c1 34100 80000 12*0 12 c1 34400 80000 12*0 12 c1 3d100 80000 12*0 12 c1 3e400
  //   80000 204*0 12 c1 30100 80000 12*0 12 c1 30400 80000 12*0 12 c1 3b100 80000 12*0 12 c1 3b400 80000
  //   204*0 12 c1 12 44 80000 11*0 12 c1 12 50 44 80000 10*0 12 c1 204 80000 12*0 12 c1 804 80000 204*0 12
  //   c1 12 1 80000 11*0 12 c1 12 50 1 80000 10*0 12 c1 1 80000 12*0 12 c1 1 80000 204*0 12 c1 12 44 80000
  //   11*0 12 c1 12 50 44 80000 10*0 12 c1 204 80000 12*0 12 c1 804 80000 2492*0 12 c1 8 80000 12*0 12 c1
  //   12 40041 80000 11*0 12 c1 12 50 40041 80000 10*0 12 c1 40200 80000 12*0 12 c1 40800 80000 204*0 12
  //   c1 12 141 80000 11*0 12 c1 12 441 80000 11*0 12 c1 12 50 141 80000 10*0 12 c1 12 50 441 80000 10*0
  //   12 c1 12 50 221 80000 10*0 12 c1 12 50 821 80000 170*0 12 c1 34100 80000 12*0 12 c1 34400 80000 12*0
  //   12 c1 3d100 80000 12*0 12 c1 3e400 80000 204*0 12 c1 30100 80000 12*0 12 c1 30400 80000 12*0 12 c1
  //   3b100 80000 12*0 12 c1 3b400 80000 204*0 12 c1 12 44 80000 11*0 12 c1 12 50 44 80000 10*0 12 c1 204
  //   80000 12*0 12 c1 804 80000 204*0 12 c1 12 44 80000 11*0 12 c1 12 50 44 80000 10*0 12 c1 204 80000
  //   12*0 12 c1 804 80000 204*0 12 c1 12 1 80000 11*0 12 c1 12 50 1 80000 10*0 12 c1 1 80000 12*0 12 c1 1
  //   80000 2492*0 12 c1 8 80000 12*0 12 c1 12 40041 80000 11*0 12 c1 12 50 40041 80000 10*0 12 c1 40200
  //   80000 12*0 12 c1 40800 80000 204*0 12 c1 12 141 80000 11*0 12 c1 12 441 80000 11*0 12 c1 12 50 141
  //   80000 10*0 12 c1 12 50 441 80000 10*0 12 c1 12 50 221 80000 10*0 12 c1 12 50 821 80000 170*0 12 c1
  //   34100 80000 12*0 12 c1 34400 80000 12*0 12 c1 3d100 80000 12*0 12 c1 3e400 80000 204*0 12 c1 30100
  //   80000 12*0 12 c1 30400 80000 12*0 12 c1 3b100 80000 12*0 12 c1 3b400 80000 204*0 12 c1 12 44 80000
  //   11*0 12 c1 12 50 44 80000 10*0 12 c1 204 80000 12*0 12 c1 804 80000 204*0 12 c1 12 44 80000 11*0 12
  //   c1 12 50 44 80000 10*0 12 c1 204 80000 12*0 12 c1 804 80000 204*0 12 c1 12 44 80000 11*0 12 c1 12 50
  //   44 80000 10*0 12 c1 204 80000 12*0 12 c1 804 80000
  //   DISPLAY REGISTER
  //   A & B REGISTER, ALU, FLAG REGISTER
endmodule

module MPU (
  input  in_1,
  input  in_2
);

  wire C_out, clock_1_out, E_out;
  wire [1:0] mcu_1_flg;
  wire [5:0] mcu_1_tmo;
  wire [7:0] binairy_to_bcd_converter_1_p2, counter_1_q, mcu_1_addr, mcu_1_data, mcu_1_pc, mcu_1_reg_a,
       mcu_1_reg_b, rom_1_data;

  ROM rom_1 (.addr(counter_1_q), .data(rom_1_data));
  Counter #(.ongoal("stay")) counter_1 (
    .count(1'b1), .Q(counter_1_q), .up(1'b1), .clk(clock_1_out), .clr(C_out));  // open: load, D, carry
  Clock clock_1 (.out(clock_1_out));
  _7_Segment_Display u_7_segment_display_1 ();  // open: g, f, a, b, e, d, c, dp
  // BCD_to_7_Segment_decoder bcd_to_7_segment_decoder_1: pin names not known
  // Binairy_to_BCD_converter #(.binvalue(8)) binairy_to_bcd_converter_1: pin names not known; wires that end beside it: clock_1_out, binairy_to_bcd_converter_1_p2
  Button E (.out(E_out));
  Button C (.out(C_out));
  _7_Segment_Display u_7_segment_display_2 ();  // open: g, f, a, b, e, d, c, dp
  _7_Segment_Display u_7_segment_display_3 ();  // open: g, f, a, b, e, d, c, dp
  // BCD_to_7_Segment_decoder bcd_to_7_segment_decoder_2: pin names not known
  // BCD_to_7_Segment_decoder bcd_to_7_segment_decoder_3: pin names not known
  MCU mcu_1 (
    .DISP(binairy_to_bcd_converter_1_p2), .FLG(mcu_1_flg), .PC(mcu_1_pc), .TMO(mcu_1_tmo), .ADDR(mcu_1_addr),
    .DATA(mcu_1_data), .REG_A(mcu_1_reg_a), .REG_B(mcu_1_reg_b), .DBG(in_2), .CLK(clock_1_out), .ENT(E_out),
    .DI(rom_1_data), .AI(counter_1_q), .PROG(in_1), .CLR(C_out));
  LED led_1 (.in(mcu_1_pc[7]));
  LED led_2 (.in(mcu_1_pc[6]));
  LED led_3 (.in(mcu_1_pc[5]));
  LED led_4 (.in(mcu_1_pc[4]));
  LED led_5 (.in(mcu_1_reg_a[7]));
  LED led_6 (.in(mcu_1_reg_a[6]));
  LED led_7 (.in(mcu_1_reg_a[5]));
  LED led_8 (.in(mcu_1_reg_a[4]));
  LED led_9 (.in(mcu_1_addr[7]));
  LED led_10 (.in(mcu_1_addr[6]));
  LED led_11 (.in(mcu_1_addr[5]));
  LED led_12 (.in(mcu_1_addr[4]));
  LED led_13 (.in(mcu_1_pc[1]));
  LED led_14 (.in(mcu_1_pc[0]));
  LED led_15 (.in(mcu_1_pc[3]));
  LED led_16 (.in(mcu_1_pc[2]));
  LED led_17 (.in(mcu_1_reg_a[1]));
  LED led_18 (.in(mcu_1_reg_a[0]));
  LED led_19 (.in(mcu_1_reg_a[3]));
  LED led_20 (.in(mcu_1_reg_a[2]));
  LED led_21 (.in(mcu_1_addr[1]));
  LED led_22 (.in(mcu_1_addr[0]));
  LED led_23 (.in(mcu_1_addr[3]));
  LED led_24 (.in(mcu_1_addr[2]));
  LED led_25 (.in(mcu_1_tmo[5]));
  LED led_26 (.in(mcu_1_tmo[4]));
  LED led_27 (.in(mcu_1_tmo[3]));
  LED led_28 (.in(mcu_1_reg_b[7]));
  LED led_29 (.in(mcu_1_reg_b[6]));
  LED led_30 (.in(mcu_1_reg_b[5]));
  LED led_31 (.in(mcu_1_data[7]));
  LED led_32 (.in(mcu_1_data[6]));
  LED led_33 (.in(mcu_1_data[5]));
  LED led_34 (.in(mcu_1_tmo[2]));
  LED led_35 (.in(mcu_1_tmo[1]));
  LED led_36 (.in(mcu_1_tmo[0]));
  LED led_37 (.in(mcu_1_reg_b[4]));
  LED led_38 (.in(mcu_1_reg_b[3]));
  LED led_39 (.in(mcu_1_reg_b[2]));
  LED led_40 (.in(mcu_1_reg_b[1]));
  LED led_41 (.in(mcu_1_data[4]));
  LED led_42 (.in(mcu_1_data[3]));
  LED led_43 (.in(mcu_1_data[2]));
  LED led_44 (.in(mcu_1_data[1]));
  LED led_45 (.in(mcu_1_reg_b[0]));
  LED led_46 (.in(mcu_1_flg[1]));
  LED led_47 (.in(mcu_1_flg[0]));
  LED led_48 (.in(mcu_1_data[0]));

  // Notes on the sheet:
  //   contents of rom_1 (hex, n*v repeats v):
  //   11 11 12 22 21 23 15 3a 2 3a
endmodule
